# Fritzing sketch LDR (saved by Fritzing 1.0.1rc)
breadboards: 1

parts:
  Part1 = Arduino Uno (Rev3) - ICSP
  LED1 = LED - 5mm [color="Red (633nm)" current=0.030A package="5 mm [THT]"]
  R1 = Resistor [tolerance=±5% resistance=220 power=0.25W package=THT]
  R2 = Resistor [tolerance=±5% resistance=10k power=0.25W package=THT]
  R3 = Photocell (LDR) [package=THT]

nets:
  N1: Part1.A0, R2.Pin_0, R3.pin_1
  N2: Part1.5V, R2.Pin_1
  N3: Part1.D13/SCK, R1.Pin_0
  N4: Part1.GND, LED1.cathode, R3.pin_0
  N5: LED1.anode, R1.Pin_1

// code stored in the sketch: LDR.ino
// Project 9? Light the lamp
int LED = 13;                      //define LED digital pin 13
int val = 0;                       //define the voltage value of photo diode in
digital pin 0
void setup(){
    pinMode(LED,OUTPUT);           // Configure LED as output mode
    Serial.begin(9600);            //Configure baud rate 9600
}
void loop(){
    val = analogRead(0); // Read voltage value ranging from 0 -1023
    Serial.println(val);   // read voltage value from serial monitor
    if(val<1000){          // If lower than 1000, turn off LED
        digitalWrite(LED,LOW);
    }else{                         // Otherwise turn on LED
        digitalWrite(LED,HIGH);
    }
    delay(10);                     // delay for 10ms
}
