# Fritzing sketch RCL_Shield (saved by Fritzing 0.9.6b)

parts:
  Part1 = Adafruit Proto Shield R3 [part_number="Adafruit #2077"]
  Adafruit_QT_5V_to_3V_Shifter1 = Adafruit QT 5V to 3V Shifter Breakout [part_number=#5637]
  Part2 = Adafruit Precision 9-DoF LIS3MDL + LSM6DSOX [part_number="Adafruit #4517"]

nets:
  N1: Part1.1#0, Part1.P$5#1, Part1.A5, Adafruit_QT_5V_to_3V_Shifter1.SCL
  GND: Part1.GND, Part1.P$5#161, Part1.1#163, Part1.P$5#164, Adafruit_QT_5V_to_3V_Shifter1.GND
  +5V: Part1.+5V, Part1.P$5#170, Part1.1#205, Part1.P$5#206, Adafruit_QT_5V_to_3V_Shifter1.VCC
  3.3V: Part1.3.3V, Part1.P$5#167, Part1.1#202, Part1.P$5#203, Adafruit_QT_5V_to_3V_Shifter1.3.3V
  N2: Part1.A4, Part1.1#117, Part1.P$5#118, Adafruit_QT_5V_to_3V_Shifter1.SDA
  N3: Part1.1#120, Part1.P$5#121, Part1.P$6#122, Part1.N$10, Part1.N$42, Part1.N$218, Part1.N$270, Part2.VCC, Part2.SDA
  N4: Part1.N$155, Part2.ADAG
  N5: Part1.P$5#194, Part1.P$6#195, Adafruit_QT_5V_to_3V_Shifter1.SDA_3V
  N6: Part1.N$7, Part2.ADM
  N7: Part1.N$81, Part2.INTM
  N8: Part1.N$100, Part2.DRDY
  N9: Part1.N$105, Part2.INT1
  N10: Part1.N$226, Part2.INT2
  N11: Part1.N$258, Part2.3.3V
  N12: Part1.N$266, Part2.SCL
  N13: Part1.N$269, Part2.GND

custom parts:
  Adafruit Proto Shield R3: This prototyping shield is the best out there (well, we think so, at least), and now is even better with Version R3 - updated for the most compatibility with just about all the Arduinos! It works with UNO, Mega, Leonardo, NG, Diecimila, Duemilanove, and compatible Arduinos. Yun's and Arduino Ethernets have a chunky Ethernet jack that gets in the way of stacking, you can use the stacking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
  Adafruit QT 5V to 3V Shifter Breakout: If you're hankerin' to use the new Qwiic / Stemma QT standard for your next project - but you're still using a classic Arduino UNO or other 5V microcontroller, this board is designed for you! Note that Adafruit QT boards are all 3V and 5V safe but many other Qwiic and other I2C devices are not 5V safe or compatible. That means that if you use wires to connect a Qwiic board to a 5V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
  Adafruit Precision 9-DoF LIS3MDL + LSM6DSOX: Add high quality motion, direction and orientation sensing to your Arduino project with this all-in-one 9 Degree of Freedom (9-DoF) sensor with sensors from ST. This little breakout contains two chips that sit side-by-side to provide 9 degrees of full-motion data. The board includes an LSM6DSOX, a 6-DoF IMU accelerometer + gyro. The 3-axis accelerometer can tell you which direction is down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
